# Fritzing sketch pritz project ph reader (saved by Fritzing 0.9.3b)
breadboards: 1

parts:
  Componente1 = Arduino Nano (Rev3.0)
  pH_Circuit1 = pH Circuit

nets:
  GND: Componente1.GND, pH_Circuit1.GND
  5V: Componente1.5V, pH_Circuit1.Vcc
  N1: Componente1.A0, pH_Circuit1.RX

custom parts:
  pH Circuit: Ph circuit designs that are available on the Internet today are antiquated and use a significant number of overly complex analog components. Atlas Scientific has reinvented and refined the pH Circuit of yesteryear. The Atlas Scientific pH Circuit is our fifth generation pH Circuit. The Atlas Scientific pH Circuit enables the engineer to easily incorporate scientific grade pH monitoring into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

// code stored in the sketch: main.ino
// pHRead.ino

// Constants:-
const byte pHpin = A0;// Connect the sensor's Po output to analogue pin 0.

// Variables:-
float Po;

void setup()
{
Serial.begin(9600);
}

void loop()
{
Po = (1023 - analogRead(pHpin)) / 73.07; // Read and reverse the analogue input value from the pH sensor then scale 0-14.
Serial.println(Po, 2);// Print the result in the serial monitor.
delay(1000);// Take 1 reading per second.
}
